// Digital circuit ALU_com_display.dig as structural Verilog
module ALU_com_display (
  input  [7:0] A,
  input  [7:0] B,
  input  [2:0] seletor,
  output overflow
);

  wire of_shiftleft, of_shiftright, of_somador, of_subtrator;
  wire [7:0] \and , multiplexer_1_out, \or , Produto, shift_left, shift_right, somador, subtrator, \xor ;

  somador_8_bits somador_8_bits_1 (.A(A), .B(B), .overflow(of_somador), .S(somador));
  subtrator8bit subtrator8bit_1 (.A(A), .B(B), .overflow(of_subtrator), .S(subtrator));
  multiplicador multiplicador_1 (.A(A[3:0]), .B(B[3:0]), .P(Produto));
  shift_left shift_left_1 (.entrada(A), .overflow(of_shiftleft), .shift_left(shift_left));
  shift_right shift_right_1 (.entrada(B), .overflow(of_shiftright), .shift_right(shift_right));
  assign \and  = A & B;  // And and_1, 8 bits wide
  assign \or  = A | B;  // Or or_1, 8 bits wide
  assign \xor  = A ^ B;  // XOr xor_1, 8 bits wide
  or or_2 (overflow, of_somador, of_shiftleft, of_shiftright, of_subtrator);
  Multiplexer #(.Selector_Bits(3), .Bits(8)) multiplexer_1 (
    .sel(seletor), .in_0(somador), .in_1(subtrator), .in_2(Produto), .in_3(shift_left), .in_4(shift_right),
    .in_5(\and ), .in_6(\or ), .in_7(\xor ), .out(multiplexer_1_out));
  Seven_Seg_Hex seven_seg_hex_1 (.d(multiplexer_1_out[7:4]), .dp(1'b0));
  Seven_Seg_Hex seven_seg_hex_2 (.d(multiplexer_1_out[3:0]), .dp(1'b0));

  // Other names for the same wires on the sheet: A_m[3:0] = A[3:0]; B_m[3:0] = B[3:0]

  // Notes on the sheet:
  //   0: Somador, soma os valores entre A e B
  //   1: Subtrador, subtrai os valores entre B e A
  //   2: Multiplicador, multiplica os valores entre A e B
  //   3: shift left, desloca os bits para a esquerda
  //   4: shift right, desloca os bits para a direita
  //   5: AND, operação bit a bit AND
  //   6: OR, operação bit a bit OR
  //   5: XOR, operação bit a bit XOR
endmodule
