// Digital circuit CPU.dig as structural Verilog
module CPU (
  input  [2:0] PC,
  output overflow
);

  wire C;
  wire [7:0] ALU_saida, B;
  wire [10:0] eepromdualport_1_d;

  Button button_1 (.out(C));
  EEPROMDualPort #(.AddrBits(3), .Bits(11)) eepromdualport_1 (
    .A(PC), .Din({11{1'b0}}), .str(1'b0), .C(C), .ld(1'b1), .D(eepromdualport_1_d));
  Seven_Seg_Hex seven_seg_hex_1 (.d(B[7:4]), .dp(1'b0));
  ALU alu_1 (
    .A(eepromdualport_1_d[10:3]), .B(B), .seletor(eepromdualport_1_d[2:0]), .overflow(overflow), .S(ALU_saida));
  Seven_Seg_Hex seven_seg_hex_2 (.d(B[3:0]), .dp(1'b0));
  Register #(.Bits(8)) register_1 (.D(ALU_saida), .C(C), .en(1'b1), .Q(B));

  // Notes on the sheet:
  //   contents of eepromdualport_1 (hex, n*v repeats v):
  //   8,9,12,3,5,4,6,7
endmodule
