// Digital circuit FullAdder.dig as structural Verilog
module FullAdder (
  input  A,
  input  B,
  input  carry_in,
  output S,
  output carry_out
);

  wire and_1_out, and_2_out, xor_2_out;

  and and_1 (and_1_out, B, A);
  or or_1 (carry_out, and_2_out, and_1_out);
  and and_2 (and_2_out, carry_in, xor_2_out);
  xor xor_1 (S, xor_2_out, carry_in);
  xor xor_2 (xor_2_out, B, A);
endmodule
