// Digital circuit and.dig as structural Verilog
module \and  (
  input  in_1,
  input  in_2,
  input  in_3,
  input  in_4,
  input  in_5,
  input  in_6,
  input  in_7,
  input  in_8,
  input  in_9,
  input  in_10,
  input  in_11,
  input  in_12,
  input  in_13,
  input  in_14,
  input  in_15,
  input  in_16,
  input  in_25,
  input  in_26,
  input  in_28,
  input  in_29,
  input  in_31,
  input  in_32,
  input  in_34,
  input  in_35,
  input  in_37,
  input  in_38,
  input  in_40,
  input  in_41,
  input  in_43,
  input  in_44,
  input  in_46,
  input  in_47,
  input  in_49,
  input  in_50,
  input  in_52,
  input  in_53,
  input  in_55,
  input  in_56,
  input  in_58,
  input  in_59,
  input  in_61,
  input  in_62,
  input  in_64,
  input  in_65,
  input  in_67,
  input  in_68,
  input  in_70,
  input  in_71,
  output out_17,
  output out_18,
  output out_19,
  output out_20,
  output out_21,
  output out_22,
  output out_23,
  output out_24,
  output out_27,
  output out_30,
  output out_33,
  output out_36,
  output out_39,
  output out_42,
  output out_45,
  output out_48,
  output out_51,
  output out_54,
  output out_57,
  output out_60,
  output out_63,
  output out_66,
  output out_69,
  output out_72
);

  and and_1 (out_17, in_1, in_2);
  and and_2 (out_18, in_3, in_4);
  and and_3 (out_19, in_5, in_6);
  and and_4 (out_20, in_7, in_8);
  and and_5 (out_21, in_9, in_10);
  and and_6 (out_22, in_11, in_12);
  and and_7 (out_23, in_13, in_14);
  and and_8 (out_24, in_15, in_16);
  or or_1 (out_27, in_25, in_26);
  or or_2 (out_30, in_28, in_29);
  or or_3 (out_33, in_31, in_32);
  or or_4 (out_36, in_34, in_35);
  or or_5 (out_39, in_37, in_38);
  or or_6 (out_42, in_40, in_41);
  or or_7 (out_45, in_43, in_44);
  or or_8 (out_48, in_46, in_47);
  xor xor_1 (out_51, in_49, in_50);
  xor xor_2 (out_54, in_52, in_53);
  xor xor_3 (out_57, in_55, in_56);
  xor xor_4 (out_60, in_58, in_59);
  xor xor_5 (out_63, in_61, in_62);
  xor xor_6 (out_66, in_64, in_65);
  xor xor_7 (out_69, in_67, in_68);
  xor xor_8 (out_72, in_70, in_71);
endmodule
