// Digital circuit multiplicador.dig as structural Verilog
module multiplicador (
  input  [3:0] A,
  input  [3:0] B,
  output [7:0] P
);

  wire and_1_out, and_2_out, and_3_out, and_4_out, and_5_out, and_6_out, and_7_out, and_8_out, and_9_out,
       and_10_out, and_11_out, and_12_out, and_13_out, and_14_out, and_15_out, fulladder_2_carry_out,
       fulladder_2_s, fulladder_3_carry_out, fulladder_4_carry_out, fulladder_4_s, fulladder_5_carry_out,
       fulladder_5_s, fulladder_6_carry_out, fulladder_7_carry_out, fulladder_7_s, fulladder_8_carry_out,
       fulladder_8_s, fulladder_9_carry_out, fulladder_10_carry_out, fulladder_10_s, fulladder_11_carry_out,
       fulladder_12_carry_out;

  FullAdder fulladder_1 (
    .A(and_1_out), .B(fulladder_2_carry_out), .carry_in(fulladder_3_carry_out), .S(P[6]), .carry_out(P[7]));
  and and_1 (and_1_out, A[3], B[3]);
  FullAdder fulladder_2 (
    .A(and_3_out), .B(fulladder_4_carry_out), .carry_in(fulladder_5_carry_out), .S(fulladder_2_s),
    .carry_out(fulladder_2_carry_out));
  FullAdder fulladder_3 (
    .A(and_4_out), .B(fulladder_2_s), .carry_in(fulladder_6_carry_out), .S(P[5]),
    .carry_out(fulladder_3_carry_out));
  and and_2 (and_2_out, A[3], B[1]);
  FullAdder fulladder_4 (
    .A(fulladder_7_carry_out), .B(and_2_out), .carry_in(1'b0), .S(fulladder_4_s),
    .carry_out(fulladder_4_carry_out));
  and and_3 (and_3_out, A[3], B[2]);
  and and_4 (and_4_out, A[2], B[3]);
  and and_5 (and_5_out, A[2], B[2]);
  FullAdder fulladder_5 (
    .A(and_5_out), .B(fulladder_4_s), .carry_in(fulladder_8_carry_out), .S(fulladder_5_s),
    .carry_out(fulladder_5_carry_out));
  and and_6 (and_6_out, A[1], B[3]);
  FullAdder fulladder_6 (
    .A(and_6_out), .B(fulladder_5_s), .carry_in(fulladder_9_carry_out), .S(P[4]),
    .carry_out(fulladder_6_carry_out));
  and and_7 (and_7_out, A[2], B[1]);
  FullAdder fulladder_7 (
    .A(and_8_out), .B(and_7_out), .carry_in(fulladder_10_carry_out), .S(fulladder_7_s),
    .carry_out(fulladder_7_carry_out));
  FullAdder fulladder_8 (
    .A(and_10_out), .B(fulladder_7_s), .carry_in(fulladder_11_carry_out), .S(fulladder_8_s),
    .carry_out(fulladder_8_carry_out));
  FullAdder fulladder_9 (
    .A(and_11_out), .B(fulladder_8_s), .carry_in(1'b0), .S(P[3]), .carry_out(fulladder_9_carry_out));
  and and_8 (and_8_out, A[3], B[0]);
  and and_9 (and_9_out, A[1], B[1]);
  and and_10 (and_10_out, A[1], B[2]);
  and and_11 (and_11_out, A[0], B[3]);
  and and_12 (and_12_out, A[2], B[0]);
  FullAdder fulladder_10 (
    .A(and_12_out), .B(and_9_out), .carry_in(fulladder_12_carry_out), .S(fulladder_10_s),
    .carry_out(fulladder_10_carry_out));
  FullAdder fulladder_11 (
    .A(and_14_out), .B(fulladder_10_s), .carry_in(1'b0), .S(P[2]), .carry_out(fulladder_11_carry_out));
  and and_13 (and_13_out, A[0], B[1]);
  and and_14 (and_14_out, A[0], B[2]);
  and and_15 (and_15_out, A[1], B[0]);
  FullAdder fulladder_12 (
    .A(and_15_out), .B(and_13_out), .carry_in(1'b0), .S(P[1]), .carry_out(fulladder_12_carry_out));
  and and_16 (P[0], A[0], B[0]);

  // Other names for the same wires on the sheet: A_0 = A[0]; A_1 = A[1]; A_2 = A[2]; A_3 = A[3]; B_0 = B[0];
  //   B_1 = B[1]; B_2 = B[2]; B_3 = B[3]; P_0 = P[0]; P_1 = P[1]; P_2 = P[2]; P_3 = P[3]; P_4 = P[4]; P_5 = P[5];
  //   P_6 = P[6]; P_7 = P[7]
endmodule
