// Digital circuit or.dig as structural Verilog
module \or  (
  input  in_1,
  input  in_2,
  input  in_4,
  input  in_5,
  input  in_7,
  input  in_8,
  input  in_10,
  input  in_11,
  input  in_13,
  input  in_14,
  input  in_16,
  input  in_17,
  input  in_19,
  input  in_20,
  input  in_22,
  input  in_23,
  output out_3,
  output out_6,
  output out_9,
  output out_12,
  output out_15,
  output out_18,
  output out_21,
  output out_24
);

  or or_1 (out_3, in_1, in_2);
  or or_2 (out_6, in_4, in_5);
  or or_3 (out_9, in_7, in_8);
  or or_4 (out_12, in_10, in_11);
  or or_5 (out_15, in_13, in_14);
  or or_6 (out_18, in_16, in_17);
  or or_7 (out_21, in_19, in_20);
  or or_8 (out_24, in_22, in_23);
endmodule
