// Digital circuit shift_left.dig as structural Verilog
module shift_left (
  input  [7:0] entrada,
  output overflow,
  output [7:0] shift_left
);


  assign overflow = entrada[0];
  assign shift_left = {1'b0, entrada[7:1]};
endmodule
