// Digital circuit shift_right.dig as structural Verilog
module shift_right (
  input  [7:0] entrada,
  output overflow,
  output [7:0] shift_right
);


  assign overflow = entrada[7];
  assign shift_right = {entrada[6:0], 1'b0};
endmodule
