// Digital circuit somador-8-bits.dig as structural Verilog
module somador_8_bits (
  input  [7:0] A,
  input  [7:0] B,
  output overflow,
  output [7:0] S
);

  wire fulladder_1_carry_out, fulladder_2_carry_out, fulladder_3_carry_out, fulladder_4_carry_out,
       fulladder_5_carry_out, fulladder_6_carry_out, fulladder_7_carry_out;

  FullAdder fulladder_1 (.A(A[0]), .B(B[0]), .carry_in(1'b0), .S(S[0]), .carry_out(fulladder_1_carry_out));
  FullAdder fulladder_2 (
    .A(A[1]), .B(B[1]), .carry_in(fulladder_1_carry_out), .S(S[1]), .carry_out(fulladder_2_carry_out));
  FullAdder fulladder_3 (
    .A(A[2]), .B(B[2]), .carry_in(fulladder_2_carry_out), .S(S[2]), .carry_out(fulladder_3_carry_out));
  FullAdder fulladder_4 (
    .A(A[3]), .B(B[3]), .carry_in(fulladder_3_carry_out), .S(S[3]), .carry_out(fulladder_4_carry_out));
  FullAdder fulladder_5 (
    .A(A[4]), .B(B[4]), .carry_in(fulladder_4_carry_out), .S(S[4]), .carry_out(fulladder_5_carry_out));
  FullAdder fulladder_6 (
    .A(A[5]), .B(B[5]), .carry_in(fulladder_5_carry_out), .S(S[5]), .carry_out(fulladder_6_carry_out));
  FullAdder fulladder_7 (
    .A(A[6]), .B(B[6]), .carry_in(fulladder_6_carry_out), .S(S[6]), .carry_out(fulladder_7_carry_out));
  FullAdder fulladder_8 (.A(A[7]), .B(B[7]), .carry_in(fulladder_7_carry_out), .S(S[7]), .carry_out(overflow));

  // Other names for the same wires on the sheet: A_0 = A[0]; A_1 = A[1]; A_2 = A[2]; A_3 = A[3]; A_4 = A[4];
  //   A_5 = A[5]; A_6 = A[6]; A_7 = A[7]; B_0 = B[0]; B_1 = B[1]; B_2 = B[2]; B_3 = B[3]; B_4 = B[4]; B_5 = B[5];
  //   B_6 = B[6]; B_7 = B[7]; S_0 = S[0]; S_1 = S[1]; S_2 = S[2]; S_3 = S[3]; S_4 = S[4]; S_5 = S[5]; S_6 = S[6];
  //   S_7 = S[7]
endmodule
