// Digital circuit subtrator8bit.dig as structural Verilog
module subtrator8bit (
  input  [7:0] A,
  input  [7:0] B,
  output overflow,
  output [7:0] S
);

  wire _1bitsub_1_p5, _1bitsub_2_p5, _1bitsub_3_p5, _1bitsub_4_p5, _1bitsub_5_p5, _1bitsub_6_p5,
       _1bitsub_7_p5;

  // _1bitsub _1bitsub_1: pin names not known; wires that end beside it: A[0], B[0], 1'b0, S[0], _1bitsub_1_p5
  // _1bitsub _1bitsub_2: pin names not known; wires that end beside it: A[1], B[1], _1bitsub_1_p5, S[1], _1bitsub_2_p5
  // _1bitsub _1bitsub_3: pin names not known; wires that end beside it: A[2], B[2], _1bitsub_2_p5, S[2], _1bitsub_3_p5
  // _1bitsub _1bitsub_4: pin names not known; wires that end beside it: A[3], B[3], _1bitsub_3_p5, S[3], _1bitsub_4_p5
  // _1bitsub _1bitsub_5: pin names not known; wires that end beside it: A[4], B[4], _1bitsub_4_p5, S[4], _1bitsub_5_p5
  // _1bitsub _1bitsub_6: pin names not known; wires that end beside it: A[5], B[5], _1bitsub_5_p5, S[5], _1bitsub_6_p5
  // _1bitsub _1bitsub_7: pin names not known; wires that end beside it: A[6], B[6], _1bitsub_6_p5, S[6], _1bitsub_7_p5
  // _1bitsub _1bitsub_8: pin names not known; wires that end beside it: A[7], B[7], _1bitsub_7_p5, S[7], overflow

  // Other names for the same wires on the sheet: A_0 = A[0]; A_1 = A[1]; A_2 = A[2]; A_3 = A[3]; A_4 = A[4];
  //   A_5 = A[5]; A_6 = A[6]; A_7 = A[7]; B_0 = B[0]; B_1 = B[1]; B_2 = B[2]; B_3 = B[3]; B_4 = B[4]; B_5 = B[5];
  //   B_6 = B[6]; B_7 = B[7]; S_0 = S[0]; S_1 = S[1]; S_2 = S[2]; S_3 = S[3]; S_4 = S[4]; S_5 = S[5]; S_6 = S[6];
  //   S_7 = S[7]
endmodule
