// Digital circuit xor.dig as structural Verilog
module \xor  (
  input  in_1,
  input  in_2,
  input  in_4,
  input  in_5,
  input  in_7,
  input  in_8,
  input  in_10,
  input  in_11,
  input  in_13,
  input  in_14,
  input  in_16,
  input  in_17,
  input  in_19,
  input  in_20,
  input  in_22,
  input  in_23,
  output out_3,
  output out_6,
  output out_9,
  output out_12,
  output out_15,
  output out_18,
  output out_21,
  output out_24
);

  xor xor_1 (out_3, in_1, in_2);
  xor xor_2 (out_6, in_4, in_5);
  xor xor_3 (out_9, in_7, in_8);
  xor xor_4 (out_12, in_10, in_11);
  xor xor_5 (out_15, in_13, in_14);
  xor xor_6 (out_18, in_16, in_17);
  xor xor_7 (out_21, in_19, in_20);
  xor xor_8 (out_24, in_22, in_23);
endmodule
